// Logisim project cse332_project.circ as structural Verilog
module main (
  output Write_Enable,
  output [15:0] read_data_1,
  output [15:0] \output ,
  output Cin,
  output B_invert,
  output [15:0] read_data_2,
  output [15:0] shifted_value,
  output [1:0] operation,
  output Reg_Dst,
  output MemToReg,
  output [15:0] immediate,
  output [15:0] Write_Data,
  output ALUSrc,
  output sw,
  output lw,
  output SLL_SRL,
  output [3:0] opcode,
  output [3:0] RS,
  output [3:0] RT,
  output [3:0] RD,
  output Shift,
  output zero,
  output overflow,
  output Cout
);

  wire clock, reset;
  wire [3:0] RD_RT;
  wire [15:0] adder_1_out, Data, RAM_data, Reg_Imm, register_1_q;

  Multiplexer #(.width(4)) multiplexer_1 (.in0(RD), .in1(RT), .out(RD_RT), .sel(Reg_Dst));  // open: en
  Multiplexer #(.width(16)) multiplexer_2 (.in0(\output ), .in1(RAM_data), .out(Data), .sel(MemToReg));  // open: en
  Adder #(.width(16)) adder_1 (.a(register_1_q), .b(16'h1), .out(adder_1_out));  // open: cin, cout
  Register #(.width(16)) register_1 (.D(adder_1_out), .Q(register_1_q), .clk(clock), .clr(reset));  // open: en
  Clock u_clock (.out(clock));
  Button u_reset (.out(reset));
  Multiplexer #(.width(16)) multiplexer_3 (
    .in0(read_data_2), .in1(immediate), .out(Reg_Imm), .sel(ALUSrc));  // open: en
  Multiplexer #(.width(16)) multiplexer_4 (.in0(Data), .in1(shifted_value), .out(Write_Data), .sel(Shift));  // open: en
  ROM #(.addrWidth(16), .dataWidth(16)) rom_1 (.addr(register_1_q), .data({opcode, RS, RT, RD}));  // open: sel
  _16bit_control_unit u_16bit_control_unit_1 (
    .in_1(opcode), .Reg_Dst(Reg_Dst), .Write_En(Write_Enable), .ALUSrc(ALUSrc), .C_in(Cin),
    .B_invert(B_invert), .lw(lw), .sw(sw), .MemToReg(MemToReg), .Shift(Shift), .SLL_SRL(SLL_SRL),
    .ALU_Op(operation));
  _16_bit_register_file_ic_with_zero u_16_bit_register_file_ic_with_zero_1 (
    .Write_Data(Write_Data), .Write_Enable(Write_Enable), .RS(RS), .RT(RT), .Read_Data_1(read_data_1),
    .Read_Data_2(read_data_2), .Clock(clock), .Reset(reset), .Destination__RD(RD_RT));
  assign immediate = {{12{1'b0}}, RD};  // Bit_Extender bit_extender_1
  _16_bit_alu u_16_bit_alu_1 (
    .B_invert(B_invert), .Cin(Cin), .Output(operation), .A(read_data_1), .B(Reg_Imm), .output_2(\output ),
    .zero(zero), .Cout(Cout), .overflow(overflow));
  Shift shift_1 (.Data(read_data_1), .Shift_ammount(RD), .SLL_SRL(SLL_SRL), .Output(shifted_value));
  RAM #(.addrWidth(16), .dataWidth(16), .bus("separate")) ram_1 (
    .addr(\output ), .din(read_data_2), .data(RAM_data), .str(sw), .clk(clock), .ld(lw), .clr(reset));  // open: sel

  // Other names for the same wires on the sheet: imm[15:0] = immediate; Write_En = Write_Enable

  // Notes on the sheet:
  //   MULTIPLEXERS
  //   contents of rom_1 (hex, n*v repeats v):
  //   123 5013 5125 512a 5121 5123 5123
  //   OUTPUTS
endmodule

module _16bit_register_file_ic (
  input  Clock,
  input  Reset,
  input  [15:0] Write_Data,
  input  Write_Enable,
  input  [3:0] Destination__RD,
  input  [3:0] RS,
  input  [3:0] RT,
  output [15:0] Read_Data_1,
  output [15:0] Read_Data_2
);

  wire demultiplexer_1_out0, demultiplexer_1_out1, demultiplexer_1_out2, demultiplexer_1_out3,
       demultiplexer_1_out4, demultiplexer_1_out5, demultiplexer_1_out6, demultiplexer_1_out7,
       demultiplexer_1_out8, demultiplexer_1_out9, demultiplexer_1_out10, demultiplexer_1_out11,
       demultiplexer_1_out12, demultiplexer_1_out13, demultiplexer_1_out14, demultiplexer_1_out15;
  wire [15:0] r0_q, r1_q, r2_q, r3_q, r4_q, r5_q, r6_q, r7_q, r8_q, r9_q, r10_q, r11_q, r12_q, r13_q, r14_q,
       r15_q;

  Demultiplexer #(.select(4)) demultiplexer_1 (
    .out0(demultiplexer_1_out0), .out1(demultiplexer_1_out1), .out2(demultiplexer_1_out2),
    .out3(demultiplexer_1_out3), .out4(demultiplexer_1_out4), .out5(demultiplexer_1_out5),
    .out6(demultiplexer_1_out6), .out7(demultiplexer_1_out7), .out8(demultiplexer_1_out8),
    .out9(demultiplexer_1_out9), .out10(demultiplexer_1_out10), .out11(demultiplexer_1_out11),
    .out12(demultiplexer_1_out12), .out13(demultiplexer_1_out13), .out14(demultiplexer_1_out14),
    .out15(demultiplexer_1_out15), .in(Write_Enable), .sel(Destination__RD));  // open: en
  Register #(.width(16)) r0 (.D(Write_Data), .en(demultiplexer_1_out0), .Q(r0_q), .clk(Clock), .clr(Reset));
  Register #(.width(16)) r1 (.D(Write_Data), .en(demultiplexer_1_out1), .Q(r1_q), .clk(Clock), .clr(Reset));
  Register #(.width(16)) r2 (.D(Write_Data), .en(demultiplexer_1_out2), .Q(r2_q), .clk(Clock), .clr(Reset));
  Register #(.width(16)) r3 (.D(Write_Data), .en(demultiplexer_1_out3), .Q(r3_q), .clk(Clock), .clr(Reset));
  Register #(.width(16)) r4 (.D(Write_Data), .en(demultiplexer_1_out4), .Q(r4_q), .clk(Clock), .clr(Reset));
  Register #(.width(16)) r5 (.D(Write_Data), .en(demultiplexer_1_out5), .Q(r5_q), .clk(Clock), .clr(Reset));
  Register #(.width(16)) r6 (.D(Write_Data), .en(demultiplexer_1_out6), .Q(r6_q), .clk(Clock), .clr(Reset));
  Register #(.width(16)) r7 (.D(Write_Data), .en(demultiplexer_1_out7), .Q(r7_q), .clk(Clock), .clr(Reset));
  Register #(.width(16)) r8 (.D(Write_Data), .en(demultiplexer_1_out8), .Q(r8_q), .clk(Clock), .clr(Reset));
  Register #(.width(16)) r9 (.D(Write_Data), .en(demultiplexer_1_out9), .Q(r9_q), .clk(Clock), .clr(Reset));
  Register #(.width(16)) r10 (.D(Write_Data), .en(demultiplexer_1_out10), .Q(r10_q), .clk(Clock), .clr(Reset));
  Register #(.width(16)) r11 (.D(Write_Data), .en(demultiplexer_1_out11), .Q(r11_q), .clk(Clock), .clr(Reset));
  Register #(.width(16)) r12 (.D(Write_Data), .en(demultiplexer_1_out12), .Q(r12_q), .clk(Clock), .clr(Reset));
  Register #(.width(16)) r13 (.D(Write_Data), .en(demultiplexer_1_out13), .Q(r13_q), .clk(Clock), .clr(Reset));
  Register #(.width(16)) r14 (.D(Write_Data), .en(demultiplexer_1_out14), .Q(r14_q), .clk(Clock), .clr(Reset));
  Register #(.width(16)) r15 (.D(Write_Data), .en(demultiplexer_1_out15), .Q(r15_q), .clk(Clock), .clr(Reset));
  Multiplexer #(.select(4), .width(16)) multiplexer_1 (
    .in0(r0_q), .in1(r1_q), .in2(r2_q), .in3(r3_q), .in4(r4_q), .in5(r5_q), .in6(r6_q), .in7(r7_q),
    .in8(r8_q), .in9(r9_q), .in10(r10_q), .in11(r11_q), .in12(r12_q), .in13(r13_q), .in14(r14_q),
    .in15(r15_q), .out(Read_Data_1), .sel(RS));  // open: en
  Multiplexer #(.select(4), .width(16)) multiplexer_2 (
    .in0(r0_q), .in1(r1_q), .in2(r2_q), .in3(r3_q), .in4(r4_q), .in5(r5_q), .in6(r6_q), .in7(r7_q),
    .in8(r8_q), .in9(r9_q), .in10(r10_q), .in11(r11_q), .in12(r12_q), .in13(r13_q), .in14(r14_q),
    .in15(r15_q), .out(Read_Data_2), .sel(RT));  // open: en
endmodule

module _16_bit_register_file_ic_with_zero (
  input  Clock,
  input  Reset,
  input  [15:0] Write_Data,
  input  Write_Enable,
  input  [3:0] Destination__RD,
  input  [3:0] RS,
  input  [3:0] RT,
  output [15:0] Read_Data_1,
  output [15:0] Read_Data_2
);

  wire demultiplexer_1_out0, demultiplexer_1_out1, demultiplexer_1_out2, demultiplexer_1_out3,
       demultiplexer_1_out4, demultiplexer_1_out5, demultiplexer_1_out6, demultiplexer_1_out7,
       demultiplexer_1_out8, demultiplexer_1_out9, demultiplexer_1_out10, demultiplexer_1_out11,
       demultiplexer_1_out12, demultiplexer_1_out13, demultiplexer_1_out14, demultiplexer_1_out15;
  wire [15:0] s0_q, s1_q, s2_q, s3_q, s4_q, s5_q, t0_q, t1_q, t2_q, t3_q, t4_q, t5_q, t6_q, t7_q, t8_q,
       zero_q;

  Demultiplexer #(.select(4)) demultiplexer_1 (
    .out0(demultiplexer_1_out0), .out1(demultiplexer_1_out1), .out2(demultiplexer_1_out2),
    .out3(demultiplexer_1_out3), .out4(demultiplexer_1_out4), .out5(demultiplexer_1_out5),
    .out6(demultiplexer_1_out6), .out7(demultiplexer_1_out7), .out8(demultiplexer_1_out8),
    .out9(demultiplexer_1_out9), .out10(demultiplexer_1_out10), .out11(demultiplexer_1_out11),
    .out12(demultiplexer_1_out12), .out13(demultiplexer_1_out13), .out14(demultiplexer_1_out14),
    .out15(demultiplexer_1_out15), .in(Write_Enable), .sel(Destination__RD));  // open: en
  Register #(.width(16)) zero (.D({16{1'b0}}), .en(demultiplexer_1_out0), .Q(zero_q), .clk(Clock), .clr(Reset));
  Register #(.width(16)) t0 (.D(Write_Data), .en(demultiplexer_1_out1), .Q(t0_q), .clk(Clock), .clr(Reset));
  Register #(.width(16)) t1 (.D(Write_Data), .en(demultiplexer_1_out2), .Q(t1_q), .clk(Clock), .clr(Reset));
  Register #(.width(16)) t2 (.D(Write_Data), .en(demultiplexer_1_out3), .Q(t2_q), .clk(Clock), .clr(Reset));
  Register #(.width(16)) t3 (.D(Write_Data), .en(demultiplexer_1_out4), .Q(t3_q), .clk(Clock), .clr(Reset));
  Register #(.width(16)) s0 (.D(Write_Data), .en(demultiplexer_1_out5), .Q(s0_q), .clk(Clock), .clr(Reset));
  Register #(.width(16)) s1 (.D(Write_Data), .en(demultiplexer_1_out6), .Q(s1_q), .clk(Clock), .clr(Reset));
  Register #(.width(16)) s2 (.D(Write_Data), .en(demultiplexer_1_out7), .Q(s2_q), .clk(Clock), .clr(Reset));
  Register #(.width(16)) s3 (.D(Write_Data), .en(demultiplexer_1_out8), .Q(s3_q), .clk(Clock), .clr(Reset));
  Register #(.width(16)) s4 (.D(Write_Data), .en(demultiplexer_1_out9), .Q(s4_q), .clk(Clock), .clr(Reset));
  Register #(.width(16)) s5 (.D(Write_Data), .en(demultiplexer_1_out10), .Q(s5_q), .clk(Clock), .clr(Reset));
  Register #(.width(16)) t4 (.D(Write_Data), .en(demultiplexer_1_out11), .Q(t4_q), .clk(Clock), .clr(Reset));
  Register #(.width(16)) t5 (.D(Write_Data), .en(demultiplexer_1_out12), .Q(t5_q), .clk(Clock), .clr(Reset));
  Register #(.width(16)) t6 (.D(Write_Data), .en(demultiplexer_1_out13), .Q(t6_q), .clk(Clock), .clr(Reset));
  Register #(.width(16)) t7 (.D(Write_Data), .en(demultiplexer_1_out14), .Q(t7_q), .clk(Clock), .clr(Reset));
  Register #(.width(16)) t8 (.D(Write_Data), .en(demultiplexer_1_out15), .Q(t8_q), .clk(Clock), .clr(Reset));
  Multiplexer #(.select(4), .width(16)) multiplexer_1 (
    .in0(zero_q), .in1(t0_q), .in2(t1_q), .in3(t2_q), .in4(t3_q), .in5(s0_q), .in6(s1_q), .in7(s2_q),
    .in8(s3_q), .in9(s4_q), .in10(s5_q), .in11(t4_q), .in12(t5_q), .in13(t6_q), .in14(t7_q), .in15(t8_q),
    .out(Read_Data_1), .sel(RS));  // open: en
  Multiplexer #(.select(4), .width(16)) multiplexer_2 (
    .in0(zero_q), .in1(t0_q), .in2(t1_q), .in3(t2_q), .in4(t3_q), .in5(s0_q), .in6(s1_q), .in7(s2_q),
    .in8(s3_q), .in9(s4_q), .in10(s5_q), .in11(t4_q), .in12(t5_q), .in13(t6_q), .in14(t7_q), .in15(t8_q),
    .out(Read_Data_2), .sel(RT));  // open: en
endmodule

module _1bit_alu (
  input  B_prime,
  input  A,
  input  B,
  input  Cin,
  input  [1:0] Operation,
  output out_6,
  output out_7
);

  wire adder_1_out, and_1_out, or_1_out, xor_1_out, xor_2_out;

  and and_1 (and_1_out, A, B);
  or or_1 (or_1_out, A, B);
  xor xor_1 (xor_1_out, B, B_prime);
  xor xor_2 (xor_2_out, A, B);
  Adder #(.width(1)) adder_1 (.a(A), .b(xor_1_out), .out(adder_1_out), .cin(Cin), .cout(out_7));
  Multiplexer #(.select(2)) multiplexer_1 (
    .in0(and_1_out), .in1(or_1_out), .in2(adder_1_out), .in3(xor_2_out), .out(out_6), .sel(Operation));  // open: en
endmodule

module Shift (
  input  [15:0] Data,
  input  [3:0] Shift_ammount,
  input  SLL_SRL,
  output [15:0] Output
);

  wire [15:0] shifter_1_out, shifter_2_out;

  Shifter #(.width(16)) shifter_1 (.in(Data), .\dist (Shift_ammount), .out(shifter_1_out));
  Shifter #(.width(16), .shift("lr")) shifter_2 (.in(Data), .\dist (Shift_ammount), .out(shifter_2_out));
  Multiplexer #(.width(16)) multiplexer_1 (
    .in0(shifter_1_out), .in1(shifter_2_out), .out(Output), .sel(SLL_SRL));  // open: en

  // Notes on the sheet:
  //   Shift Left Logical
  //   Shift Right Logical
endmodule

module _16_bit_alu (
  input  B_invert,
  input  Cin,
  input  [1:0] Output,
  input  [15:0] A,
  input  [15:0] B,
  output [15:0] output_2,
  output zero,
  output overflow,
  output Cout
);

  wire n1bit_alu_1_out_7, n1bit_alu_2_out_7, n1bit_alu_3_out_7, n1bit_alu_4_out_7, n1bit_alu_5_out_7,
       n1bit_alu_6_out_7, n1bit_alu_7_out_7, n1bit_alu_8_out_7, n1bit_alu_9_out_7, n1bit_alu_10_out_7,
       n1bit_alu_11_out_7, n1bit_alu_12_out_7, n1bit_alu_13_out_7, n1bit_alu_14_out_7, n1bit_alu_15_out_7;

  _1bit_alu u_1bit_alu_1 (
    .Operation(Output), .out_6(output_2[0]), .out_7(n1bit_alu_1_out_7), .B_prime(B_invert), .A(A[0]),
    .B(B[0]), .Cin(Cin));
  _1bit_alu u_1bit_alu_2 (
    .Operation(Output), .out_6(output_2[1]), .out_7(n1bit_alu_2_out_7), .B_prime(B_invert), .A(A[1]),
    .B(B[1]), .Cin(n1bit_alu_1_out_7));
  _1bit_alu u_1bit_alu_3 (
    .Operation(Output), .out_6(output_2[2]), .out_7(n1bit_alu_3_out_7), .B_prime(B_invert), .A(A[2]),
    .B(B[2]), .Cin(n1bit_alu_2_out_7));
  _1bit_alu u_1bit_alu_4 (
    .Operation(Output), .out_6(output_2[3]), .out_7(n1bit_alu_4_out_7), .B_prime(B_invert), .A(A[3]),
    .B(B[3]), .Cin(n1bit_alu_3_out_7));
  _1bit_alu u_1bit_alu_5 (
    .Operation(Output), .out_6(output_2[4]), .out_7(n1bit_alu_5_out_7), .B_prime(B_invert), .A(A[4]),
    .B(B[4]), .Cin(n1bit_alu_4_out_7));
  _1bit_alu u_1bit_alu_6 (
    .Operation(Output), .out_6(output_2[5]), .out_7(n1bit_alu_6_out_7), .B_prime(B_invert), .A(A[5]),
    .B(B[5]), .Cin(n1bit_alu_5_out_7));
  _1bit_alu u_1bit_alu_7 (
    .Operation(Output), .out_6(output_2[6]), .out_7(n1bit_alu_7_out_7), .B_prime(B_invert), .A(A[6]),
    .B(B[6]), .Cin(n1bit_alu_6_out_7));
  _1bit_alu u_1bit_alu_8 (
    .Operation(Output), .out_6(output_2[7]), .out_7(n1bit_alu_8_out_7), .B_prime(B_invert), .A(A[7]),
    .B(B[7]), .Cin(n1bit_alu_7_out_7));
  _1bit_alu u_1bit_alu_9 (
    .Operation(Output), .out_6(output_2[8]), .out_7(n1bit_alu_9_out_7), .B_prime(B_invert), .A(A[8]),
    .B(B[8]), .Cin(n1bit_alu_8_out_7));
  _1bit_alu u_1bit_alu_10 (
    .Operation(Output), .out_6(output_2[9]), .out_7(n1bit_alu_10_out_7), .B_prime(B_invert), .A(A[9]),
    .B(B[9]), .Cin(n1bit_alu_9_out_7));
  _1bit_alu u_1bit_alu_11 (
    .Operation(Output), .out_6(output_2[10]), .out_7(n1bit_alu_11_out_7), .B_prime(B_invert), .A(A[10]),
    .B(B[10]), .Cin(n1bit_alu_10_out_7));
  _1bit_alu u_1bit_alu_12 (
    .Operation(Output), .out_6(output_2[11]), .out_7(n1bit_alu_12_out_7), .B_prime(B_invert), .A(A[11]),
    .B(B[11]), .Cin(n1bit_alu_11_out_7));
  _1bit_alu u_1bit_alu_13 (
    .Operation(Output), .out_6(output_2[12]), .out_7(n1bit_alu_13_out_7), .B_prime(B_invert), .A(A[12]),
    .B(B[12]), .Cin(n1bit_alu_12_out_7));
  _1bit_alu u_1bit_alu_14 (
    .Operation(Output), .out_6(output_2[13]), .out_7(n1bit_alu_14_out_7), .B_prime(B_invert), .A(A[13]),
    .B(B[13]), .Cin(n1bit_alu_13_out_7));
  _1bit_alu u_1bit_alu_15 (
    .Operation(Output), .out_6(output_2[14]), .out_7(n1bit_alu_15_out_7), .B_prime(B_invert), .A(A[14]),
    .B(B[14]), .Cin(n1bit_alu_14_out_7));
  _1bit_alu u_1bit_alu_16 (
    .Operation(Output), .out_6(output_2[15]), .out_7(Cout), .B_prime(B_invert), .A(A[15]), .B(B[15]),
    .Cin(n1bit_alu_15_out_7));
  xor xor_1 (overflow, n1bit_alu_15_out_7, Cout);
  nor nor_1 (zero, output_2[0], output_2[1], output_2[2], output_2[3], output_2[4], output_2[5], output_2[6], output_2[7], output_2[8], output_2[9], output_2[10], output_2[11], output_2[12], output_2[13], output_2[14], output_2[15]);

  // Other names for the same wires on the sheet: _0 = output_2[0]; _1 = output_2[1]; _2 = output_2[2];
  //   _3 = output_2[3]; _4 = output_2[4]; _5 = output_2[5]; _6 = output_2[6]; _7 = output_2[7]; _8 = output_2[8];
  //   _9 = output_2[9]; _10 = output_2[10]; _11 = output_2[11]; _12 = output_2[12]; _13 = output_2[13];
  //   _14 = output_2[14]; _15 = output_2[15]
endmodule

module _16bit_alu_wtih_multiplication (
  input  B_invert,
  input  Cin,
  input  [2:0] Output,
  input  [15:0] A,
  input  [15:0] B,
  output [15:0] output_2,
  output zero,
  output [15:0] Multiplication_Couts,
  output overflow,
  output Cout
);

  wire n1bit_alu_1_p5, n1bit_alu_2_p5, n1bit_alu_3_p5, n1bit_alu_4_p5, n1bit_alu_5_p5, n1bit_alu_6_p5,
       n1bit_alu_7_p5, n1bit_alu_8_p5, n1bit_alu_9_p5, n1bit_alu_10_p5, n1bit_alu_11_p5, n1bit_alu_12_p5,
       n1bit_alu_13_p5, n1bit_alu_14_p5, n1bit_alu_15_p5;

  // _1bit_alu 1bit_alu_1: pin names not known; wires that end beside it: Output, A[0], B[0], B_invert, n1bit_alu_1_p5, Cin, output_2[0], Multiplication_Couts[0]
  // _1bit_alu 1bit_alu_2: pin names not known; wires that end beside it: Output, A[1], B[1], B_invert, n1bit_alu_2_p5, n1bit_alu_1_p5, Multiplication_Couts[0], output_2[1], Multiplication_Couts[1]
  // _1bit_alu 1bit_alu_3: pin names not known; wires that end beside it: Output, A[2], B[2], B_invert, n1bit_alu_3_p5, n1bit_alu_2_p5, Multiplication_Couts[1], output_2[2], Multiplication_Couts[2]
  // _1bit_alu 1bit_alu_4: pin names not known; wires that end beside it: Output, A[3], B[3], B_invert, n1bit_alu_4_p5, n1bit_alu_3_p5, Multiplication_Couts[2], output_2[3], Multiplication_Couts[3]
  // _1bit_alu 1bit_alu_5: pin names not known; wires that end beside it: Output, A[4], B[4], B_invert, n1bit_alu_5_p5, n1bit_alu_4_p5, Multiplication_Couts[3], output_2[4], Multiplication_Couts[4]
  // _1bit_alu 1bit_alu_6: pin names not known; wires that end beside it: Output, A[5], B[5], B_invert, n1bit_alu_6_p5, n1bit_alu_5_p5, Multiplication_Couts[4], output_2[5], Multiplication_Couts[5]
  // _1bit_alu 1bit_alu_7: pin names not known; wires that end beside it: Output, A[6], B[6], B_invert, n1bit_alu_7_p5, n1bit_alu_6_p5, Multiplication_Couts[5], output_2[6], Multiplication_Couts[6]
  // _1bit_alu 1bit_alu_8: pin names not known; wires that end beside it: Output, A[7], B[7], B_invert, n1bit_alu_8_p5, n1bit_alu_7_p5, Multiplication_Couts[6], output_2[7], Multiplication_Couts[7]
  // _1bit_alu 1bit_alu_9: pin names not known; wires that end beside it: Output, A[8], B[8], B_invert, n1bit_alu_9_p5, n1bit_alu_8_p5, Multiplication_Couts[7], output_2[8], Multiplication_Couts[8]
  // _1bit_alu 1bit_alu_10: pin names not known; wires that end beside it: Output, A[9], B[9], B_invert, n1bit_alu_10_p5, n1bit_alu_9_p5, Multiplication_Couts[8], output_2[9], Multiplication_Couts[9]
  // _1bit_alu 1bit_alu_11: pin names not known; wires that end beside it: Output, A[10], B[10], B_invert, n1bit_alu_11_p5, n1bit_alu_10_p5, Multiplication_Couts[9], output_2[10], Multiplication_Couts[10]
  // _1bit_alu 1bit_alu_12: pin names not known; wires that end beside it: Output, A[11], B[11], B_invert, n1bit_alu_12_p5, n1bit_alu_11_p5, Multiplication_Couts[10], output_2[11], Multiplication_Couts[11]
  // _1bit_alu 1bit_alu_13: pin names not known; wires that end beside it: Output, A[12], B[12], B_invert, n1bit_alu_13_p5, n1bit_alu_12_p5, Multiplication_Couts[11], output_2[12], Multiplication_Couts[12]
  // _1bit_alu 1bit_alu_14: pin names not known; wires that end beside it: Output, A[13], B[13], B_invert, n1bit_alu_14_p5, n1bit_alu_13_p5, Multiplication_Couts[12], output_2[13], Multiplication_Couts[13]
  // _1bit_alu 1bit_alu_15: pin names not known; wires that end beside it: Output, A[14], B[14], B_invert, n1bit_alu_15_p5, n1bit_alu_14_p5, Multiplication_Couts[13], output_2[14], Multiplication_Couts[14]
  // _1bit_alu 1bit_alu_16: pin names not known; wires that end beside it: Output, A[15], B[15], B_invert, Cout, n1bit_alu_15_p5, Multiplication_Couts[14], output_2[15], Multiplication_Couts[15]
  xor xor_1 (overflow, n1bit_alu_15_p5, Cout);
  nor nor_1 (zero, output_2[0], output_2[1], output_2[2], output_2[3], output_2[4], output_2[5], output_2[6], output_2[7], output_2[8], output_2[9], output_2[10], output_2[11], output_2[12], output_2[13], output_2[14], output_2[15]);

  // Other names for the same wires on the sheet: C0 = Multiplication_Couts[0]; C1 = Multiplication_Couts[1];
  //   C2 = Multiplication_Couts[2]; C3 = Multiplication_Couts[3]; C4 = Multiplication_Couts[4];
  //   C5 = Multiplication_Couts[5]; C6 = Multiplication_Couts[6]; C7 = Multiplication_Couts[7];
  //   C8 = Multiplication_Couts[8]; C9 = Multiplication_Couts[9]; C10 = Multiplication_Couts[10];
  //   C11 = Multiplication_Couts[11]; C12 = Multiplication_Couts[12]; C13 = Multiplication_Couts[13];
  //   C14 = Multiplication_Couts[14]; C15 = Multiplication_Couts[15]; _0 = output_2[0]; _1 = output_2[1];
  //   _2 = output_2[2]; _3 = output_2[3]; _4 = output_2[4]; _5 = output_2[5]; _6 = output_2[6]; _7 = output_2[7];
  //   _8 = output_2[8]; _9 = output_2[9]; _10 = output_2[10]; _11 = output_2[11]; _12 = output_2[12];
  //   _13 = output_2[13]; _14 = output_2[14]; _15 = output_2[15]
endmodule

module _1bit_alu_with_multiplication (
  input  B_prime,
  input  A,
  input  B,
  input  Cin,
  input  M_Cin,
  input  [2:0] Operation,
  output out_7,
  output out_8,
  output Cout
);

  wire adder_1_out, and_1_out, multiplier_1_out, or_1_out, xor_1_out, xor_2_out;

  and and_1 (and_1_out, A, B);
  or or_1 (or_1_out, A, B);
  xor xor_1 (xor_1_out, B, B_prime);
  xor xor_2 (xor_2_out, A, B);
  Multiplier #(.width(1)) multiplier_1 (.a(A), .b(B), .out(multiplier_1_out), .cin(M_Cin), .cout(Cout));
  Adder #(.width(1)) adder_1 (.a(A), .b(xor_1_out), .out(adder_1_out), .cin(Cin), .cout(out_8));
  Multiplexer #(.select(3)) multiplexer_1 (
    .in0(and_1_out), .in1(or_1_out), .in2(adder_1_out), .in3(xor_2_out), .in4(multiplier_1_out), .out(out_7),
    .sel(Operation));  // open: in5, in6, in7, en
endmodule

module _16bit_control_unit (
  input  [3:0] in_1,
  output Reg_Dst,
  output Write_En,
  output ALUSrc,
  output [1:0] ALU_Op,
  output C_in,
  output B_invert,
  output lw,
  output sw,
  output MemToReg,
  output Shift,
  output SLL_SRL
);

  wire and_1_out, and_2_out, and_3_out, and_4_out, and_5_out, and_6_out, and_7_out, and_8_out, and_9_out,
       and_10_out, and_11_out, and_12_out, and_13_out, and_14_out, and_15_out, and_16_out, and_17_out,
       and_18_out, and_19_out, and_20_out, and_21_out, and_22_out, not_1_out, not_2_out, not_3_out,
       not_4_out, not_5_out, not_6_out, not_7_out, not_8_out, not_9_out, not_10_out, not_11_out, not_12_out,
       not_13_out, not_14_out, not_15_out, not_16_out, not_17_out, not_18_out, not_19_out, not_20_out,
       not_21_out, not_22_out, not_23_out, not_24_out, not_25_out, not_26_out, not_27_out, not_28_out,
       not_29_out, not_30_out, not_31_out, not_32_out, not_33_out, not_34_out, not_35_out, not_36_out,
       not_37_out, not_38_out, not_39_out, not_40_out, not_41_out, not_42_out, not_43_out, not_44_out;

  not not_1 (not_1_out, in_1[3]);
  not not_2 (not_2_out, in_1[2]);
  not not_3 (not_3_out, in_1[1]);
  not not_4 (not_4_out, in_1[3]);
  not not_5 (not_5_out, in_1[0]);
  not not_6 (not_6_out, in_1[3]);
  not not_7 (not_7_out, in_1[1]);
  not not_8 (not_8_out, in_1[3]);
  not not_9 (not_9_out, in_1[3]);
  not not_10 (not_10_out, in_1[2]);
  not not_11 (not_11_out, in_1[1]);
  not not_12 (not_12_out, in_1[2]);
  not not_13 (not_13_out, in_1[3]);
  not not_14 (not_14_out, in_1[1]);
  not not_15 (not_15_out, in_1[3]);
  not not_16 (not_16_out, in_1[0]);
  not not_17 (not_17_out, in_1[2]);
  not not_18 (not_18_out, in_1[3]);
  not not_19 (not_19_out, in_1[2]);
  not not_20 (not_20_out, in_1[1]);
  not not_21 (not_21_out, in_1[3]);
  not not_22 (not_22_out, in_1[1]);
  not not_23 (not_23_out, in_1[0]);
  not not_24 (not_24_out, in_1[2]);
  not not_25 (not_25_out, in_1[1]);
  not not_26 (not_26_out, in_1[0]);
  not not_27 (not_27_out, in_1[2]);
  not not_28 (not_28_out, in_1[3]);
  not not_29 (not_29_out, in_1[2]);
  not not_30 (not_30_out, in_1[2]);
  not not_31 (not_31_out, in_1[0]);
  not not_32 (not_32_out, in_1[3]);
  not not_33 (not_33_out, in_1[2]);
  not not_34 (not_34_out, in_1[2]);
  not not_35 (not_35_out, in_1[0]);
  not not_36 (not_36_out, in_1[3]);
  not not_37 (not_37_out, in_1[0]);
  not not_38 (not_38_out, in_1[3]);
  not not_39 (not_39_out, in_1[1]);
  not not_40 (not_40_out, in_1[3]);
  not not_41 (not_41_out, in_1[0]);
  not not_42 (not_42_out, in_1[1]);
  not not_43 (not_43_out, in_1[1]);
  and and_1 (and_1_out, not_1_out, in_1[2], in_1[1]);
  and and_2 (and_2_out, in_1[3], not_2_out);
  and and_3 (and_3_out, in_1[3], not_3_out);
  and and_4 (and_4_out, not_4_out, not_5_out);
  not not_44 (not_44_out, in_1[2]);
  and and_5 (and_5_out, not_6_out, in_1[1]);
  and and_6 (and_6_out, in_1[3], not_7_out);
  and and_7 (and_7_out, not_8_out, in_1[2], in_1[0]);
  and and_8 (and_8_out, not_9_out, in_1[2], in_1[1]);
  and and_9 (and_9_out, in_1[3], not_10_out);
  and and_10 (and_10_out, in_1[3], not_11_out);
  and and_11 (and_11_out, not_12_out, in_1[1]);
  and and_12 (and_12_out, not_13_out, in_1[2], not_14_out);
  and and_13 (and_13_out, not_15_out, in_1[2], not_16_out);
  and and_14 (and_14_out, in_1[3], not_17_out, in_1[0]);
  and and_15 (and_15_out, not_18_out, not_19_out, not_20_out, in_1[0]);
  and and_16 (and_16_out, not_21_out, in_1[2], not_22_out, not_23_out);
  and and_17 (and_17_out, in_1[3], not_24_out, not_25_out, not_26_out);
  and and_18 (and_18_out, in_1[3], not_27_out, in_1[1], in_1[0]);
  and and_19 (and_19_out, not_28_out, not_29_out, in_1[1], in_1[0]);
  and and_20 (and_20_out, in_1[3], not_30_out, in_1[1], not_31_out);
  and and_21 (and_21_out, not_32_out, not_33_out, in_1[1], in_1[0]);
  and and_22 (and_22_out, in_1[3], not_34_out, in_1[1], not_35_out);
  and and_23 (lw, not_36_out, in_1[2], in_1[1], not_37_out);
  and and_24 (sw, not_38_out, in_1[2], not_39_out, in_1[0]);
  and and_25 (MemToReg, not_40_out, in_1[2], in_1[1], not_41_out);
  and and_26 (Shift, in_1[3], in_1[2], not_42_out);
  and and_27 (SLL_SRL, in_1[3], in_1[2], not_43_out, in_1[0]);
  or or_1 (Reg_Dst, and_1_out, and_2_out, and_3_out);
  or or_2 (Write_En, and_4_out, not_44_out, and_5_out, and_6_out);
  or or_3 (ALUSrc, and_7_out, and_8_out, and_9_out, and_10_out);
  or or_4 (ALU_Op[1], and_11_out, and_12_out, and_13_out, and_14_out);
  or or_5 (ALU_Op[0], and_15_out, and_16_out, and_17_out, and_18_out);
  or or_6 (C_in, and_19_out, and_20_out);
  or or_7 (B_invert, and_21_out, and_22_out);
endmodule
